# Fritzing sketch touchscreen_read (saved by Fritzing 0.9.3b)
breadboards: 1

parts:
  SW1 = CD4053BCN [part_number=CD4053BCN package="DIP (Dual Inline) [THT]"]
  SW1_1 = CD4053BCN [part_number=CD4053BCN package="DIP (Dual Inline) [THT]"]  # not connected
  SW1_2 = CD4053BCN [part_number=CD4053BCN package="DIP (Dual Inline) [THT]"]  # not connected
  SW1_3 = CD4053BCN [part_number=CD4053BCN package="DIP (Dual Inline) [THT]"]  # not connected
  SW1_4 = CD4053BCN [part_number=CD4053BCN package="DIP (Dual Inline) [THT]"]  # not connected
  C1 = Ceramic Capacitor [capacitance="100 nF" package="0603 [SMD, multilayer]"]
  OA1 = LMC6482AIN Dual Op-Amp [part_number=LMC6482AIN package="DIP8 [THT]"]
  OA1_3 = LMC6482AIN Dual Op-Amp [part_number=LMC6482AIN package="DIP8 [THT]"]  # not connected
  OA1_1 = LMC6482AIN Dual Op-Amp [part_number=LMC6482AIN package="DIP8 [THT]"]  # not connected
  OA1_2 = LMC6482AIN Dual Op-Amp [part_number=LMC6482AIN package="DIP8 [THT]"]  # not connected
  R1 = Resistor [tolerance=±5% resistance=10k package="1206 [SMD]"]
  R2 = Resistor [tolerance=±5% resistance=5.1k package="1206 [SMD]"]

nets:
  N1: SW1.connector0, SW1.connector15
  N2: SW1.connector1, C1.1
  N3: SW1.connector5, SW1.connector6, SW1.connector7, C1.0, OA1.connector3, R2.Pin_1
  N4: OA1.connector0, R1.Pin_0
  N5: R1.Pin_1, R2.Pin_0

notes:
  +5V from
  MSP Launchpad
  GND from
  Capacitive touchscreen
  top pad
  bottom pad
  P6.0
  22
  All sources share same GND
  +12V from
  Power Supply Unit
  P6.2
  +6V from

custom parts:
  CD4053BCN: Triple 2-Channel Analog Multiplexer/Demultiplexer
  CD4053BCN: Triple 2-Channel Analog Multiplexer/Demultiplexer
  CD4053BCN: Triple 2-Channel Analog Multiplexer/Demultiplexer
  CD4053BCN: Triple 2-Channel Analog Multiplexer/Demultiplexer
  CD4053BCN: Triple 2-Channel Analog Multiplexer/Demultiplexer
  LMC6482AIN Dual Op-Amp: Dual Rail-to-Rail Input and Output Operational Amplifier
  LMC6482AIN Dual Op-Amp: Dual Rail-to-Rail Input and Output Operational Amplifier
  LMC6482AIN Dual Op-Amp: Dual Rail-to-Rail Input and Output Operational Amplifier
  LMC6482AIN Dual Op-Amp: Dual Rail-to-Rail Input and Output Operational Amplifier
